// Logisim project cpu_logisim.circ as structural Verilog
module instruction_fetch (
  input  [15:0] pc_in,
  output [2:0] alu_op
);

  wire [7:0] rom_1_p2;

  // ROM #(.addrWidth(15), .line("quad")) rom_1: pin names not known; wires that end beside it: pc_in[14:0], rom_1_p2
endmodule

module register_file (
  input  we_in_1,
  input  [1:0] in_sel_1,
  input  out_en_1,
  input  [1:0] sel_out_1,
  input  we_in_2,
  input  [1:0] in_sel_2,
  input  out_en_2,
  input  [1:0] sel_out_2,
  input  res,
  output [7:0] output_1,
  output [7:0] output_2
);

  wire clock_1_out, clock_2_out, clock_3_out, clock_4_out, comparator_1_eq, decoder_1_out0, decoder_1_out1,
       decoder_1_out2, decoder_1_out3, decoder_2_out0, decoder_2_out1, decoder_2_out2, decoder_2_out3,
       decoder_3_out0, decoder_3_out1, decoder_3_out2, decoder_3_out3, decoder_4_out0, decoder_4_out1,
       decoder_4_out2, decoder_4_out3, or_1_out, or_2_out, or_3_out, or_4_out;
  wire [7:0] controlled_buffer_1_out, controlled_buffer_3_out, controlled_buffer_5_out,
       controlled_buffer_7_out, register_1_q, register_2_q, register_3_q, register_4_q, undriven, undriven_2;

  Comparator #(.mode("unsigned"), .width(2)) comparator_1 (
    .a(in_sel_1), .b(in_sel_2), .eq(comparator_1_eq));  // open: gt, lt
  Decoder #(.select(2)) decoder_1 (
    .out0(decoder_1_out0), .out1(decoder_1_out1), .out2(decoder_1_out2), .out3(decoder_1_out3),
    .sel(in_sel_1), .en(we_in_1));
  Decoder #(.select(2)) decoder_2 (
    .out0(decoder_2_out0), .out1(decoder_2_out1), .out2(decoder_2_out2), .out3(decoder_2_out3),
    .sel(in_sel_2), .en(we_in_2));
  // AND_Gate and_1 has open pins: in0=comparator_1_eq, in1=we_in_2, in2=we_in_1, out=open
  assign controlled_buffer_1_out = decoder_1_out0 ? undriven : 8'bz;  // Controlled_Buffer controlled_buffer_1
  assign controlled_buffer_1_out = decoder_2_out0 ? undriven_2 : 8'bz;  // Controlled_Buffer controlled_buffer_2
  assign controlled_buffer_3_out = decoder_1_out1 ? undriven : 8'bz;  // Controlled_Buffer controlled_buffer_3
  assign controlled_buffer_3_out = decoder_2_out1 ? undriven_2 : 8'bz;  // Controlled_Buffer controlled_buffer_4
  assign controlled_buffer_5_out = decoder_1_out2 ? undriven : 8'bz;  // Controlled_Buffer controlled_buffer_5
  assign controlled_buffer_5_out = decoder_2_out2 ? undriven_2 : 8'bz;  // Controlled_Buffer controlled_buffer_6
  assign controlled_buffer_7_out = decoder_1_out3 ? undriven : 8'bz;  // Controlled_Buffer controlled_buffer_7
  assign controlled_buffer_7_out = decoder_2_out3 ? undriven_2 : 8'bz;  // Controlled_Buffer controlled_buffer_8
  Register register_1 (.D(controlled_buffer_1_out), .en(or_1_out), .clk(clock_1_out), .Q(register_1_q), .clr(res));
  or or_1 (or_1_out, decoder_1_out0, decoder_2_out0);
  Clock clock_1 (.out(clock_1_out));
  Register register_2 (.D(controlled_buffer_3_out), .en(or_2_out), .clk(clock_2_out), .Q(register_2_q), .clr(res));
  or or_2 (or_2_out, decoder_1_out1, decoder_2_out1);
  Clock clock_2 (.out(clock_2_out));
  Register register_3 (.D(controlled_buffer_5_out), .en(or_3_out), .clk(clock_3_out), .Q(register_3_q), .clr(res));
  or or_3 (or_3_out, decoder_1_out2, decoder_2_out2);
  Clock clock_3 (.out(clock_3_out));
  Register register_4 (.D(controlled_buffer_7_out), .en(or_4_out), .clk(clock_4_out), .Q(register_4_q), .clr(res));
  or or_4 (or_4_out, decoder_1_out3, decoder_2_out3);
  Clock clock_4 (.out(clock_4_out));
  assign output_1 = decoder_3_out0 ? register_1_q : 8'bz;  // Controlled_Buffer controlled_buffer_9
  assign output_2 = decoder_4_out0 ? register_1_q : 8'bz;  // Controlled_Buffer controlled_buffer_10
  assign output_1 = decoder_3_out1 ? register_2_q : 8'bz;  // Controlled_Buffer controlled_buffer_11
  assign output_2 = decoder_4_out1 ? register_2_q : 8'bz;  // Controlled_Buffer controlled_buffer_12
  assign output_1 = decoder_3_out2 ? register_3_q : 8'bz;  // Controlled_Buffer controlled_buffer_13
  assign output_2 = decoder_4_out2 ? register_3_q : 8'bz;  // Controlled_Buffer controlled_buffer_14
  assign output_1 = decoder_3_out3 ? register_4_q : 8'bz;  // Controlled_Buffer controlled_buffer_15
  assign output_2 = decoder_4_out3 ? register_4_q : 8'bz;  // Controlled_Buffer controlled_buffer_16
  Decoder #(.select(2)) decoder_3 (
    .out0(decoder_3_out0), .out1(decoder_3_out1), .out2(decoder_3_out2), .out3(decoder_3_out3),
    .sel(sel_out_1), .en(out_en_1));
  Decoder #(.select(2)) decoder_4 (
    .out0(decoder_4_out0), .out1(decoder_4_out1), .out2(decoder_4_out2), .out3(decoder_4_out3),
    .sel(sel_out_2), .en(out_en_2));
endmodule

module alu (
  input  [3:0] flags_i,
  input  [7:0] input_1,
  input  [7:0] input_2,
  input  [1:0] alu_op,
  input  shift,
  input  singel_operand,
  output flags_o
);

  wire adder_1_cout;
  wire [7:0] adder_1_out, and_1_out, multiplexer_1_out, not_1_out, or_1_out, xor_1_out;

  Adder adder_1 (.a(input_1), .b(input_2), .out(adder_1_out), .cout(adder_1_cout));  // open: cin
  assign and_1_out = input_1 & input_2;  // AND_Gate and_1, 8 bits wide
  assign or_1_out = input_1 | input_2;  // OR_Gate or_1, 8 bits wide
  assign xor_1_out = input_1 ^ input_2;  // XOR_Gate xor_1, 8 bits wide
  assign not_1_out = ~input_1;  // NOT_Gate not_1, 8 bits wide
  Multiplexer #(.select(2), .width(8)) multiplexer_1 (
    .in0(adder_1_out), .in1(and_1_out), .in2(or_1_out), .in3(xor_1_out), .out(multiplexer_1_out));  // open: sel
  Adder adder_2 (.a(not_1_out));  // open: b, out, cin, cout
  Multiplexer #(.width(8)) multiplexer_2 (.in0(multiplexer_1_out));  // open: in1, out, sel
  Multiplexer #(.select(2), .width(8)) multiplexer_3 (.in0(not_1_out));  // open: in1, in2, in3, out, sel
endmodule
